# Fritzing sketch SmartLCDandIOexpander_I2c_wiring (saved by Fritzing 0.9.3b)

parts:
  LCD1 = LCD screen
  Part1 = Arduino Nano (Rev3.0)
  Part2 = Arduino Nano (Rev3.0)
  R1 = Trimmer Potentiometer [maximum_resistance=10kΩ package=THT]
  R3 = Resistor [tolerance=±5% resistance=10k package=THT]
  R4 = Resistor [tolerance=±5% resistance=10k package=THT]
  R5 = Resistor [tolerance=±5% resistance=1.0k package=THT]
  S1 = Toggle Switch [package=THT]

nets:
  GND: LCD1.VSS, LCD1.R/W, LCD1.LED-, Part1.GND, Part2.GND, R1.leg2, R5.Pin_0
  5V: LCD1.VDD, Part1.5V, Part2.5V
  N1: LCD1.V0, R1.wiper
  N2: LCD1.RS, Part1.D2
  N3: LCD1.E, Part1.D4
  N4: LCD1.DB4, Part1.D5
  N5: LCD1.DB5, Part1.D6
  N6: LCD1.DB6, Part1.D7
  N7: LCD1.DB7, Part1.D8
  N8: LCD1.LED+, Part1.D9
  N9: Part1.D3, S1.COM
  N10: Part1.A5, Part2.A5, R4.Pin_0
  N11: Part1.A4, Part2.A4, R3.Pin_0
  N12: Part2.3V3, R3.Pin_1, R4.Pin_1
  N13: R5.Pin_1, S1.L2

notes:
  Optional select alt I2C port address
  LCD Contrast
  SmartLCDandIOexpander_Serial_Test
  SmartLCDandIOexpander_Serial_Backpack
  1.0K
  10k
  I2C Bus
  Power normally supplied from this port
  Master
  Slave
  Unused I/O pins can be read and written to
  by master controller
